// Logisim project ex2.circ as structural Verilog: 6 circuits, main circuit AND2
module AND2 (
  input  A,
  input  B,
  output RESULT
);

  and and_1 (RESULT, A, B);

  // Notes on the sheet:
  //   Sample Circuit
endmodule

module NAND2 (
  input  A,
  input  B,
  output RESULT
);

  wire and_1_out;

  and and_1 (and_1_out, A, B);
  not not_1 (RESULT, and_1_out);
endmodule

module NOR2 (
  input  A,
  input  B,
  output RESULT
);

  wire or_1_out;

  or or_1 (or_1_out, A, B);
  not not_1 (RESULT, or_1_out);
endmodule

module XOR2 (
  input  A,
  input  B,
  output RESULT
);

  wire and_1_out, and_2_out, not_1_out, not_2_out;

  not not_1 (not_1_out, A);
  not not_2 (not_2_out, B);
  and and_1 (and_1_out, not_1_out, B);
  and and_2 (and_2_out, A, not_2_out);
  or or_1 (RESULT, and_1_out, and_2_out);
endmodule

module MUX2 (
  input  A,
  input  B,
  input  SEL,
  output RESULT
);

  wire and_1_out, and_2_out, and_3_out, not_1_out, or_1_out;

  and and_1 (and_1_out, A, B);
  not not_1 (not_1_out, SEL);
  and and_2 (and_2_out, B, SEL);
  and and_3 (and_3_out, A, not_1_out);
  or or_1 (or_1_out, and_3_out, and_2_out);
  or or_2 (RESULT, and_1_out, or_1_out);
endmodule

module MUX4 (
  input  A,
  input  B,
  input  C,
  input  D,
  input  SEL0,
  input  SEL1,
  output RESULT
);

  wire and_1_out, and_2_out, and_3_out, and_4_out, and_5_out, and_6_out, and_7_out, and_8_out, and_9_out,
       and_10_out, and_11_out, not_1_out, not_2_out, or_1_out, or_2_out, or_3_out;

  not not_1 (not_1_out, SEL0);
  not not_2 (not_2_out, SEL1);
  and and_1 (and_1_out, not_1_out, not_2_out);
  and and_2 (and_2_out, SEL0, not_2_out);
  and and_3 (and_3_out, not_1_out, SEL1);
  and and_4 (and_4_out, SEL0, SEL1);
  and and_5 (and_5_out, A, B);
  and and_6 (and_6_out, C, D);
  and and_7 (and_7_out, A, and_1_out);
  and and_8 (and_8_out, B, and_2_out);
  and and_9 (and_9_out, C, and_3_out);
  and and_10 (and_10_out, D, and_4_out);
  and and_11 (and_11_out, and_5_out, and_6_out);
  or or_1 (or_1_out, and_9_out, and_10_out);
  or or_2 (or_2_out, and_11_out, and_7_out);
  or or_3 (or_3_out, and_8_out, or_1_out);
  or or_4 (RESULT, or_2_out, or_3_out);
endmodule
